# Fritzing sketch ChickenDoor (saved by Fritzing 0.9.4)
circuit board: 8.48706cm x 5.84835cm
breadboards: 1

parts:
  Part1 = Itsy Bitsy 32u4 5V @ 16MHz [part_number="Adafruit #3677"]
  IC1 = ULN2803A [package=THT]
  JACK1 = 2.1mm DC Barrel Jack
  Door_Lock = Solenoid
  Door_Lift = Adafruit Gear-Reduced Stepper Motor (small)
  Light_Meter = Adafruit GA1A1S202WP [part_number="Adafruit #1384"]
  Motor_FET = Basic FET N-Channel [package="TO220 [THT]"]
  R1 = Resistor [tolerance=±5% resistance=220 package=THT]
  s-door-closed = Pushbutton [package=THT]
  s-door-open = Pushbutton [package=THT]

nets:
  N1: Part1.D4, R1.Pin_0
  GND: Part1.GND, JACK1.switch, Light_Meter.GND, Motor_FET.source, s-door-closed.leg1, s-door-open.leg1
  N2: Part1.VBAT, IC1.COM_-_Common, JACK1.center, Door_Lock.pin2, Door_Lift.RED, Light_Meter.VCC
  N3: Part1.D11, IC1.In_1
  N4: Part1.D10, IC1.In_2
  N5: Part1.D9, IC1.In_3
  N6: Part1.D7, IC1.In_4
  N7: Part1.D1, IC1.In_7, IC1.In_8
  N8: Part1.A4, Light_Meter.OUT
  N9: Part1.A2, s-door-open.leg0
  N10: Part1.A1, s-door-closed.leg0
  N11: IC1.0V, Motor_FET.drain
  N12: IC1.Out_8, IC1.Out_7, Door_Lock.pin1
  N13: IC1.Out_4, Door_Lift.BLUE
  N14: IC1.Out_3, Door_Lift.PINK
  N15: IC1.Out_2, Door_Lift.YELLOW
  N16: IC1.Out_1, Door_Lift.ORANGE
  N17: Motor_FET.gate, R1.Pin_1

custom parts:
  Itsy Bitsy 32u4 5V @ 16MHz: What's smaller than a Feather but larger than a Trinket? It's an Itsy Bitsy! Small, powerful, Arduino-compatible - this microcontroller board is perfect when you want something very compact, but still with a bunch of pins. Itsy Bitsy is only 1.4" long by 0.7" wide, but has 6 power pins, 6 analog & digital pins and 17 digital pins. It packs much of the same capability as an Arduino UNO. So it's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
  2.1mm DC Barrel Jack: 2.1mm DC Barrel Jack with Thru-Hole Connectors (breadboardable)
  Adafruit Gear-Reduced Stepper Motor (small): Adafruit gear-reduction stepper motor (small)
  Adafruit GA1A1S202WP: Upgrade a project that uses a photocell with the GA1A12S202 analog light sensor. Like a CdS photo-cell, the sensor does not require a microcontroller, the analog voltage output increases with the amount of light shining on the sensor face. This sensor has a lot of improvements that make it better for nearly any project. The biggest improvement over plain photocells is a true log-lin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
